# Fritzing sketch temperature_sensor (saved by Fritzing 0.9.3b)
breadboards: 1

parts:
  Raspberry_Pi_1 = Raspberry Pi 3 [part_number=RPI-3-V1.2]
  ADC1 = MCP3008 [package=dil16]
  T1 = TMP36 Temperature Sensor [package="TO92 [THT]"]

nets:
  3V3: Raspberry_Pi_1.3v3, ADC1.VREF, ADC1.VDD, T1.+Vs
  N1: Raspberry_Pi_1.GPIO10, ADC1.Din
  N2: Raspberry_Pi_1.GPIO9, ADC1.Dout
  N3: Raspberry_Pi_1.GPIO11, ADC1.CLK
  N4: Raspberry_Pi_1.GPIO8, ADC1.CS/SHDN
  GND: Raspberry_Pi_1.GND, ADC1.DGND, ADC1.AGND, T1.GND
  N5: ADC1.CH0, T1.Vout
